# Fritzing sketch 06.huzzzah_esp8266_dht22 (saved by Fritzing 0.9.3b)
breadboards: 1

parts:
  Composant1 = Adafruit Feather HUZZAH ESP8266 [part_number="Adafruit #2821"]
  DHT1 = DHT22 Humidity and Temperature Sensor
  R1 = Resistor [tolerance=±5% resistance=10k package=THT]

nets:
  GND: Composant1.GND, DHT1.GND
  3.3V: Composant1.3.3V, DHT1.VDD, R1.Pin_1
  N1: Composant1.GPIO5/SCL, DHT1.DATA, R1.Pin_0

custom parts:
  Adafruit Feather HUZZAH ESP8266: his is the Adafruit Feather HUZZAH ESP8266 - our take on an 'all-in-one' ESP8266 WiFi development board with built in USB and battery charging. Its an ESP8266 WiFi module with all the extras you need, ready to rock! We have other boards in the Feather family, check'em out here. At the Feather HUZZAH's heart is an ESP8266 WiFi microcontroller clocked at 80 MHz and at 3.3V logic. This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
